# Fritzing sketch KonohaSquadSchema (saved by Fritzing 0.9.3b)
breadboards: 1

parts:
  Raspberry_Pi_1 = Raspberry Pi 3 [part_number=RPI-3-V1.2]
  MOTOR1 = 28BYJ-48 Stepper Motor
  ULN2003A_-_Stepper_Driver_Board1 = ULN2003A - Stepper Driver Board [package=board]
  MOTOR2 = 28BYJ-48 Stepper Motor
  MOTOR3 = 28BYJ-48 Stepper Motor
  ULN2003A_-_Stepper_Driver_Board2 = ULN2003A - Stepper Driver Board [package=board]
  ULN2003A_-_Stepper_Driver_Board3 = ULN2003A - Stepper Driver Board [package=board]
  U1 = BATTERY-2 [package=battery-aaa]

nets:
  N1: Raspberry_Pi_1.GPIO4, Raspberry_Pi_1.GPIO14, ULN2003A_-_Stepper_Driver_Board2.IN1
  N2: Raspberry_Pi_1.GPIO17, Raspberry_Pi_1.GPIO18, ULN2003A_-_Stepper_Driver_Board2.IN2
  N3: Raspberry_Pi_1.GPIO27, Raspberry_Pi_1.GND, ULN2003A_-_Stepper_Driver_Board2.IN3
  N4: Raspberry_Pi_1.GPIO22, Raspberry_Pi_1.GPIO23, ULN2003A_-_Stepper_Driver_Board2.IN4
  N5: Raspberry_Pi_1.GPIO6, ULN2003A_-_Stepper_Driver_Board3.IN1
  N6: Raspberry_Pi_1.GPIO13, ULN2003A_-_Stepper_Driver_Board3.IN2
  N7: Raspberry_Pi_1.GPIO19, ULN2003A_-_Stepper_Driver_Board3.IN3
  N8: Raspberry_Pi_1.GPIO26, ULN2003A_-_Stepper_Driver_Board3.IN4
  N9: Raspberry_Pi_1.GPIO21, ULN2003A_-_Stepper_Driver_Board1.IN4
  N10: Raspberry_Pi_1.GPIO20, ULN2003A_-_Stepper_Driver_Board1.IN3
  N11: Raspberry_Pi_1.GPIO16, ULN2003A_-_Stepper_Driver_Board1.IN2
  N12: Raspberry_Pi_1.GPIO12, ULN2003A_-_Stepper_Driver_Board1.IN1
  N13: MOTOR1.RED, ULN2003A_-_Stepper_Driver_Board1.RED
  N14: MOTOR1.ORANGE, ULN2003A_-_Stepper_Driver_Board1.ORANGE
  N15: MOTOR1.YELLOW, ULN2003A_-_Stepper_Driver_Board1.YELLOW
  N16: MOTOR1.PINK, ULN2003A_-_Stepper_Driver_Board1.PINK
  N17: MOTOR1.BLUE, ULN2003A_-_Stepper_Driver_Board1.BLUE
  GND: ULN2003A_-_Stepper_Driver_Board1.GND, ULN2003A_-_Stepper_Driver_Board2.GND, ULN2003A_-_Stepper_Driver_Board3.GND, U1.+2
  VCC: ULN2003A_-_Stepper_Driver_Board1.VCC, ULN2003A_-_Stepper_Driver_Board2.VCC, ULN2003A_-_Stepper_Driver_Board3.VCC, U1.-2
  N18: MOTOR2.RED, ULN2003A_-_Stepper_Driver_Board2.RED
  N19: MOTOR2.ORANGE, ULN2003A_-_Stepper_Driver_Board2.ORANGE
  N20: MOTOR2.YELLOW, ULN2003A_-_Stepper_Driver_Board2.YELLOW
  N21: MOTOR2.PINK, ULN2003A_-_Stepper_Driver_Board2.PINK
  N22: MOTOR2.BLUE, ULN2003A_-_Stepper_Driver_Board2.BLUE
  N23: MOTOR3.RED, ULN2003A_-_Stepper_Driver_Board3.RED
  N24: MOTOR3.ORANGE, ULN2003A_-_Stepper_Driver_Board3.ORANGE
  N25: MOTOR3.YELLOW, ULN2003A_-_Stepper_Driver_Board3.YELLOW
  N26: MOTOR3.PINK, ULN2003A_-_Stepper_Driver_Board3.PINK
  N27: MOTOR3.BLUE, ULN2003A_-_Stepper_Driver_Board3.BLUE

notes:
  12 V supply with minimum of 1.8 A

custom parts:
  ULN2003A - Stepper Driver Board: A common stepper motor driver board based on ULN2003APG darlington array
